# Fritzing sketch dotnet-raspberrypi-mono (saved by Fritzing 0.9.1b)
breadboards: 1

parts:
  Raspberry_Pi1 = Raspberry Pi B rev2
  R1 = Resistor [tolerance=±5% resistance=220 package="0603 [SMD]"]
  LED1 = LED - 3mm [color="Blue (430nm)" package="3 mm [THT]"]

nets:
  N1: Raspberry_Pi1.GND, R1.Pin_0
  N2: Raspberry_Pi1.GPIO_18, LED1.cathode
  N3: R1.Pin_1, LED1.anode
